// Logisim project ALU.circ as structural Verilog: 1 circuit, main circuit main
module main (
  input  in_1,
  input  in_2,
  input  in_3,
  input  in_4,
  input  in_5,
  input  in_6
);

  wire and_1_out, and_2_out, and_6_out, and_7_out, and_8_out, and_9_out, and_10_out, and_11_out, and_12_out,
       and_13_out, not_5_out, or_1_out, undriven, xor_1_out, xor_2_out, xor_3_out;

  and and_1 (and_1_out, in_3, in_4);
  and and_2 (and_2_out, in_5, in_6);
  // NOT_Gate not_1 is placed but not wired
  xor xor_1 (xor_1_out, in_2, and_1_out);
  // NOT_Gate not_2 is placed but not wired
  // NOT_Gate not_3 is placed but not wired
  // NOT_Gate not_4 is placed but not wired
  not not_5 (not_5_out, and_2_out);
  // AND_Gate and_3 is placed but not wired
  // AND_Gate and_4 is placed but not wired
  // AND_Gate and_5 is placed but not wired
  // AND_Gate and_6 has open pins: out=and_6_out
  and and_7 (and_7_out, xor_1_out, undriven);
  buf or_1 (or_1_out, xor_1_out);  // OR_Gate
  and and_8 (and_8_out, and_6_out, xor_1_out, undriven);
  buf and_9 (and_9_out, and_7_out);  // AND_Gate
  buf and_10 (and_10_out, or_1_out);  // AND_Gate
  buf and_11 (and_11_out, not_5_out);  // AND_Gate
  xor xor_2 (xor_2_out, undriven, xor_1_out);
  // OR_Gate or_2 has open pins: in0=and_8_out, in1=and_12_out, out=open
  and and_12 (and_12_out, and_6_out, xor_2_out, in_1);
  xor xor_3 (xor_3_out, in_1, xor_2_out);
  and and_13 (and_13_out, xor_3_out, and_6_out);
  // OR_Gate or_3 has open pins: in0=and_9_out, in1=and_10_out, in2=and_11_out, in3=and_13_out, out=open
endmodule
