// Logisim project circuitosbasicos.circ as structural Verilog: 1 circuit, main circuit main
module main (
  input  A,
  input  A_2,
  input  B,
  input  B_2,
  input  A_3,
  input  A_4,
  input  B_3,
  input  B_4,
  input  A_5,
  input  A_6,
  input  B_5,
  input  B_6
);

  wire and_1_out, and_2_out, not_1_out, not_2_out, not_3_out, not_4_out, not_5_out, or_1_out, or_2_out,
       xor_1_out, xor_2_out;

  not not_1 (not_1_out, B);
  not not_2 (not_2_out, B_3);
  and and_1 (and_1_out, A, not_1_out);
  or or_1 (or_1_out, A_3, not_2_out);
  xor xor_1 (xor_1_out, A_6, B_6);
  LED led_1 (.in(and_1_out));
  LED led_2 (.in(or_1_out));
  LED led_3 (.in(not_3_out));
  not not_3 (not_3_out, xor_1_out);
  not not_4 (not_4_out, A_2);
  not not_5 (not_5_out, A_4);
  and and_2 (and_2_out, not_4_out, B_2);
  or or_2 (or_2_out, not_5_out, B_4);
  xor xor_2 (xor_2_out, A_5, B_5);
  LED led_4 (.in(and_2_out));
  LED led_5 (.in(or_2_out));
  LED led_6 (.in(xor_2_out));

  // Notes on the sheet:
  //   A = B
  //   A > B
  //   A >= B
  //   A < B
  //   A <= B
  //   A != B
endmodule
